# Fritzing sketch external.interrupt.example (saved by Fritzing 0.9.2b)
circuit board: 8.46667cm x 5.64444cm
breadboards: 1

parts:
  U3 = atmega328 [package=dip]
  C1 = Ceramic Capacitor [capacitance=100nF package="100 mil [THT, multilayer]"]
  C2 = Ceramic Capacitor [capacitance=100nF package="100 mil [THT, multilayer]"]
  U4 = Voltage Regulator - 5V [package="TO220 [THT]"]
  J1 = female pin header, 2 pins [form="♀ (female)"]
  J2 = shrouded pin header, 10 pins [form="♂ (shrouded male)"]  # not connected

nets:
  N1: U3.VCC, C2.1, U4.output_voltage
  N2: U3.GND#7, C1.0, C2.0, U4.GND, J1.pin1
  N3: C1.1, U4.input_voltage, J1.pin2
